// Digital circuit 8bit_ALU.dig as structural Verilog
module _8bit_ALU (
  input  [7:0] I1,
  input  [7:0] I2,
  input  [1:0] Op,
  output [7:0] Out,
  output Carry_add,
  output Signal_sub,
  output [7:0] Rest_div
);

  wire Cadd, Csub, demultiplexer_1_out_0, demultiplexer_1_out_1, demultiplexer_1_out_3, not_1_out;
  wire [7:0] Cdiv, Radd, Rdiv, Rmul, Rsub;

  _8bit_adder _8bit_adder_1 (.I1(I1), .I2(I2), .O(Radd), .C(Cadd));
  _8bit_multiplier _8bit_multiplier_1 (.A(I1[3:0]), .B(I2[3:0]), .O(Rmul));
  _8bit_subtractor _8bit_subtractor_1 (.I1(I1), .I2(I2), .Cin(1'b0), .O(Rsub), .C(Csub));
  _8bit_divider _8bit_divider_1 (.A(I1), .B(I2), .O(Rdiv), .R(Cdiv));
  Demultiplexer #(.Selector_Bits(2)) demultiplexer_1 (
    .sel(Op), .in(1'b1), .out_0(demultiplexer_1_out_0), .out_1(demultiplexer_1_out_1),
    .out_3(demultiplexer_1_out_3));  // open: out_2
  Multiplexer #(.Selector_Bits(2), .Bits(8)) multiplexer_1 (
    .sel(Op), .in_0(Radd), .in_1(Rsub), .in_2(Rmul), .in_3(Rdiv), .out(Out));
  Multiplexer multiplexer_2 (.sel(demultiplexer_1_out_0), .in_0(1'b0), .in_1(Cadd), .out(Carry_add));
  Multiplexer multiplexer_3 (.sel(demultiplexer_1_out_1), .in_0(1'b0), .in_1(not_1_out), .out(Signal_sub));
  not not_1 (not_1_out, Csub);
  Multiplexer #(.Bits(8)) multiplexer_4 (.sel(demultiplexer_1_out_3), .in_0({8{1'b0}}), .in_1(Cdiv), .out(Rest_div));
endmodule
