// Digital circuit 8bit_PC.dig as structural Verilog
module _8bit_PC (
  input  Cp,
  input  Clr,
  input  Ep,
  output [7:0] O
);

  wire multiplexer_2_out;
  wire [7:0] _8bit_adder_1_o, _8bit_subtractor_1_o, multiplexer_1_out, register_1_q;

  _8bit_adder _8bit_adder_1 (.I1(register_1_q), .I2(8'h1), .O(_8bit_adder_1_o));  // open: C
  _8bit_subtractor _8bit_subtractor_1 (
    .I1(_8bit_adder_1_o), .I2(_8bit_adder_1_o), .Cin(1'b0), .O(_8bit_subtractor_1_o));  // open: C
  Multiplexer #(.Bits(8)) multiplexer_1 (
    .sel(Clr), .in_0(_8bit_adder_1_o), .in_1(_8bit_subtractor_1_o), .out(multiplexer_1_out));
  Multiplexer multiplexer_2 (.sel(Clr), .in_0(Cp), .in_1(Clr), .out(multiplexer_2_out));
  Register #(.Bits(8)) register_1 (.D(multiplexer_1_out), .C(multiplexer_2_out), .en(1'b1), .Q(register_1_q));
  assign O = Ep ? register_1_q : 8'bz;  // Driver driver_1
endmodule
