// Digital circuit 8bit_adder.dig as structural Verilog
module _8bit_adder (
  input  [7:0] I1,
  input  [7:0] I2,
  output [7:0] O,
  output C
);

  wire full_adder_1_c1, full_adder_2_c1, full_adder_3_c1, full_adder_4_c1, full_adder_5_c1, full_adder_6_c1,
       full_adder_7_c1;

  Full_adder full_adder_1 (.I1(I1[0]), .I2(I2[0]), .C0(1'b0), .O(O[0]), .C1(full_adder_1_c1));
  Full_adder full_adder_2 (.I1(I1[1]), .I2(I2[1]), .C0(full_adder_1_c1), .O(O[1]), .C1(full_adder_2_c1));
  Full_adder full_adder_3 (.I1(I1[2]), .I2(I2[2]), .C0(full_adder_2_c1), .O(O[2]), .C1(full_adder_3_c1));
  Full_adder full_adder_4 (.I1(I1[3]), .I2(I2[3]), .C0(full_adder_3_c1), .O(O[3]), .C1(full_adder_4_c1));
  Full_adder full_adder_5 (.I1(I1[4]), .I2(I2[4]), .C0(full_adder_4_c1), .O(O[4]), .C1(full_adder_5_c1));
  Full_adder full_adder_6 (.I1(I1[5]), .I2(I2[5]), .C0(full_adder_5_c1), .O(O[5]), .C1(full_adder_6_c1));
  Full_adder full_adder_7 (.I1(I1[6]), .I2(I2[6]), .C0(full_adder_6_c1), .O(O[6]), .C1(full_adder_7_c1));
  Full_adder full_adder_8 (.I1(I1[7]), .I2(I2[7]), .C0(full_adder_7_c1), .O(O[7]), .C1(C));
endmodule
