// Digital circuit 8bit_divider.dig as structural Verilog
module _8bit_divider (
  input  [7:0] A,
  input  [7:0] B,
  output [7:0] O,
  output [7:0] R
);

  wire [7:0] multiplexer_1_out, multiplexer_2_out, multiplexer_3_out, multiplexer_5_out, multiplexer_6_out,
       multiplexer_7_out, multiplexer_8_out, OP0, OP1, OP2, OP3, OP4, OP5, OP6, OP7, R0, R1, R2, R3, R4, R5,
       R6, R7;

  Multiplexer #(.Bits(8)) multiplexer_1 (.sel(O[4]), .in_0(OP4), .in_1(R4), .out(multiplexer_1_out));
  _8bit_lshift _8bit_lshift_1 (.In({8{1'b0}}), .Shft(A[7]), .Out(OP7));
  _8bit_lshift _8bit_lshift_2 (.In(multiplexer_1_out), .Shft(A[3]), .Out(OP3));
  _8bit_subtractor _8bit_subtractor_1 (.I1(OP7), .I2(B), .Cin(1'b0), .O(R7), .C(O[7]));
  _8bit_subtractor _8bit_subtractor_2 (.I1(OP3), .I2(B), .Cin(1'b0), .O(R3), .C(O[3]));
  Multiplexer #(.Bits(8)) multiplexer_2 (.sel(O[7]), .in_0(OP7), .in_1(R7), .out(multiplexer_2_out));
  Multiplexer #(.Bits(8)) multiplexer_3 (.sel(O[3]), .in_0(OP3), .in_1(R3), .out(multiplexer_3_out));
  _8bit_lshift _8bit_lshift_3 (.In(multiplexer_2_out), .Shft(A[6]), .Out(OP6));
  _8bit_lshift _8bit_lshift_4 (.In(multiplexer_3_out), .Shft(A[2]), .Out(OP2));
  _8bit_subtractor _8bit_subtractor_3 (.I1(OP6), .I2(B), .Cin(1'b0), .O(R6), .C(O[6]));
  _8bit_subtractor _8bit_subtractor_4 (.I1(OP2), .I2(B), .Cin(1'b0), .O(R2), .C(O[2]));
  Multiplexer #(.Bits(8)) multiplexer_4 (.sel(O[0]), .in_0(OP0), .in_1(R0), .out(R));
  Multiplexer #(.Bits(8)) multiplexer_5 (.sel(O[6]), .in_0(OP6), .in_1(R6), .out(multiplexer_5_out));
  Multiplexer #(.Bits(8)) multiplexer_6 (.sel(O[2]), .in_0(OP2), .in_1(R2), .out(multiplexer_6_out));
  _8bit_lshift _8bit_lshift_5 (.In(multiplexer_5_out), .Shft(A[5]), .Out(OP5));
  _8bit_lshift _8bit_lshift_6 (.In(multiplexer_6_out), .Shft(A[1]), .Out(OP1));
  _8bit_subtractor _8bit_subtractor_5 (.I1(OP5), .I2(B), .Cin(1'b0), .O(R5), .C(O[5]));
  _8bit_subtractor _8bit_subtractor_6 (.I1(OP1), .I2(B), .Cin(1'b0), .O(R1), .C(O[1]));
  Multiplexer #(.Bits(8)) multiplexer_7 (.sel(O[5]), .in_0(OP5), .in_1(R5), .out(multiplexer_7_out));
  Multiplexer #(.Bits(8)) multiplexer_8 (.sel(O[1]), .in_0(OP1), .in_1(R1), .out(multiplexer_8_out));
  _8bit_lshift _8bit_lshift_7 (.In(multiplexer_7_out), .Shft(A[4]), .Out(OP4));
  _8bit_lshift _8bit_lshift_8 (.In(multiplexer_8_out), .Shft(A[0]), .Out(OP0));
  _8bit_subtractor _8bit_subtractor_7 (.I1(OP4), .I2(B), .Cin(1'b0), .O(R4), .C(O[4]));
  _8bit_subtractor _8bit_subtractor_8 (.I1(OP0), .I2(B), .Cin(1'b0), .O(R0), .C(O[0]));

  // Other names for the same wires on the sheet: Dvd0 = A[0]; Dvd1 = A[1]; Dvd2 = A[2]; Dvd3 = A[3]; Dvd4 = A[4];
  //   Dvd5 = A[5]; Dvd6 = A[6]; Dvd7 = A[7]; Div[7:0] = B
endmodule
