// Digital circuit 8bit_lshift.dig as structural Verilog
module _8bit_lshift (
  input  [7:0] In,
  input  Shft,
  output [7:0] Out
);


  assign Out = {In[6:0], Shft};

  // Other names for the same wires on the sheet: Dvd0 = In[0]; Dvd1 = In[1]; Dvd2 = In[2]; Dvd3 = In[3]; Dvd4 = In[4];
  //   Dvd5 = In[5]; Dvd6 = In[6]; Dvd7 = In[7]
endmodule
