// Digital circuit 8bit_multiplier.dig as structural Verilog
module _8bit_multiplier (
  input  [3:0] A,
  input  [3:0] B,
  output [7:0] O
);

  wire [3:0] and_1_out;
  wire [4:1] and_2_out;
  wire [5:2] and_3_out;
  wire [6:3] and_4_out;
  wire [7:0] _8bit_adder_1_o, _8bit_adder_2_o;

  and and_1 (and_1_out[3], B[3], A[0]);
  and and_2 (and_2_out[4], B[3], A[1]);
  and and_3 (and_3_out[5], B[3], A[2]);
  and and_4 (and_4_out[6], B[3], A[3]);
  and and_5 (and_1_out[2], B[2], A[0]);
  and and_6 (and_2_out[3], B[2], A[1]);
  and and_7 (and_3_out[4], B[2], A[2]);
  and and_8 (and_4_out[5], B[2], A[3]);
  and and_9 (and_1_out[1], B[1], A[0]);
  and and_10 (and_2_out[2], B[1], A[1]);
  and and_11 (and_3_out[3], B[1], A[2]);
  and and_12 (and_4_out[4], B[1], A[3]);
  and and_13 (and_1_out[0], B[0], A[0]);
  and and_14 (and_2_out[1], B[0], A[1]);
  and and_15 (and_3_out[2], B[0], A[2]);
  and and_16 (and_4_out[3], B[0], A[3]);
  _8bit_adder _8bit_adder_1 (
    .I1({4'b0000, and_1_out}), .I2({3'b000, and_2_out, 1'b0}), .O(_8bit_adder_1_o));  // open: C
  _8bit_adder _8bit_adder_2 (.I1(_8bit_adder_1_o), .I2({2'b00, and_3_out, 2'b00}), .O(_8bit_adder_2_o));  // open: C
  _8bit_adder _8bit_adder_3 (.I1(_8bit_adder_2_o), .I2({1'b0, and_4_out, 3'b000}), .O(O));  // open: C
endmodule
