// Digital circuit AutomatedRC.dig as structural Verilog
module AutomatedRC (
  input  Clk,
  output [3:0] O
);

  wire nor_1_out;
  wire [1:0] counter_1_out;

  Counter #(.Bits(2)) counter_1 (.en(1'b1), .C(Clk), .clr(1'b0), .out(counter_1_out));  // open: ovf
  nor nor_1 (nor_1_out, counter_1_out[0], counter_1_out[1]);
  CustomRingCounter customringcounter_1 (.D(nor_1_out), .Clk(Clk), .Out(O));
endmodule
