// Digital circuit CPU.dig as structural Verilog
module CPU (
  input  Clk,
  input  RC_Clk
);

  wire and_1_out, and_2_out, C_add, Cp, Ea, Ep, Eu, Exec, Fetch, NCE, NEi, NLa, NLb, NLi, NLm, NLo,
       not_1_out, not_2_out, not_3_out, not_4_out, or_1_out, S_sub, Su0, Su1;
  wire [1:0] automatedrc_1_o;
  wire [3:0] Dis0, Dis1;
  wire [7:0] AC_out, ALU_out, B_out, MAR_exec_q, MAR_fetch_q, PC_out, R_div, ROM_ins_d, ROM_var_d, W_in,
       W_out;
  wire [12:0] driver_2_out, IR_Reg_q, IR_ROM_d;

  AutomatedRC automatedrc_1 (.Clk(RC_Clk), .O({Exec, Fetch, automatedrc_1_o}));
  Register #(.Bits(8)) MAR_exec (.D(W_out), .C(~NLm), .en(Exec), .Q(MAR_exec_q));
  not not_1 (not_1_out, NCE);
  ROM #(.AddrBits(8), .Bits(8)) ROM_var (.A(MAR_exec_q), .sel(not_1_out), .D(ROM_var_d));
  and and_1 (and_1_out, ~NCE, Exec);  // And
  assign W_in = and_1_out ? ROM_var_d : 8'bz;  // Driver driver_1
  Counter #(.Bits(8)) PC (.en(1'b1), .C(Cp), .clr(not_2_out), .out(PC_out));  // open: ovf
  not not_2 (not_2_out, NEi);
  Register #(.Bits(8)) MAR_fetch (.D(W_out), .C(~NLm), .en(1'b1), .Q(MAR_fetch_q));
  not not_3 (not_3_out, NCE);
  ROM #(.AddrBits(8), .Bits(13)) IR_ROM (.A(W_out), .sel(not_4_out), .D(IR_ROM_d));
  not not_4 (not_4_out, NLi);
  assign driver_2_out = Exec ? IR_Reg_q : 13'bz;  // Driver driver_2
  Calls CC (
    .I(driver_2_out), .Rn({Exec, Fetch, automatedrc_1_o}), .Cp(Cp), .Ep(Ep), .NLm(NLm), .NCE(NCE), .NLi(NLi),
    .NEi(NEi), .NLa(NLa), .Ea(Ea), .Su0(Su0), .Eu(Eu), .NLb(NLb), .NLo(NLo), .Su1(Su1));
  assign W_in = Ep ? PC_out : 8'bz;  // Driver driver_3
  ROM #(.AddrBits(8), .Bits(8)) ROM_ins (.A(MAR_fetch_q), .sel(not_3_out), .D(ROM_ins_d));
  and and_2 (and_2_out, ~NCE, Fetch);  // And
  assign W_in = and_2_out ? ROM_ins_d : 8'bz;  // Driver driver_4
  Register #(.Bits(13)) IR_Reg (.D(IR_ROM_d), .C(Clk), .en(~NLi), .Q(IR_Reg_q));
  or or_1 (or_1_out, Ep, Ea, Eu, ~NCE);  // Or
  Register #(.Bits(8)) W_bus (.D(W_in), .C(Clk), .en(or_1_out), .Q(W_out));
  Register #(.Bits(8)) AC (.D(W_out), .C(Clk), .en(~NLa), .Q(AC_out));
  _8bit_ALU ALU (
    .I1(AC_out), .I2(B_out), .Op({Su1, Su0}), .Out(ALU_out), .Carry_add(C_add), .Signal_sub(S_sub),
    .Rest_div(R_div));
  Register #(.Bits(8)) B (.D(W_out), .C(Clk), .en(~NLb), .Q(B_out));
  Register #(.Bits(8)) Out (.D(W_out), .C(Clk), .en(~NLo), .Q({Dis1, Dis0}));
  assign W_in = Ea ? AC_out : 8'bz;  // Driver driver_5
  assign W_in = Eu ? ALU_out : 8'bz;  // Driver driver_6
  LED led_1 (.in(C_add));
  LED led_2 (.in(S_sub));
  Seven_Seg_Hex seven_seg_hex_1 (.d(Dis1), .dp(1'b0));
  Seven_Seg_Hex seven_seg_hex_2 (.d(R_div[7:4]), .dp(1'b0));
  Seven_Seg_Hex seven_seg_hex_3 (.d(Dis0), .dp(1'b0));
  Seven_Seg_Hex seven_seg_hex_4 (.d(R_div[3:0]), .dp(1'b0));

  // Notes on the sheet:
  //   Clk: Hz: 3
  //   contents of ROM_var (hex, n*v repeats v):
  //   0,1,2,3,4,5,6,7,8,9,a,b,c,d,e,f
  //   contents of IR_ROM (hex, n*v repeats v):
  //   743,bc3,5c1,583,7c6
  //   contents of ROM_ins (hex, n*v repeats v):
  //   1,2,1,3,4
endmodule
