// Digital circuit Calls.dig as structural Verilog
module Calls (
  input  [12:0] I,
  input  [3:0] Rn,
  output Cp,
  output Ep,
  output NLm,
  output NCE,
  output NLi,
  output NEi,
  output NLa,
  output Ea,
  output Su0,
  output Eu,
  output NLb,
  output NLo,
  output Su1
);

  assign {Cp, Ep, NLm, NCE, NLi, NEi, NLa, Ea, Su0, Su1, Eu, NLb, NLo} = Rn[3] ? I : 13'bz;  // Driver driver_1
  assign {Cp, Ep, NLm, NCE, NLi, NEi, NLa, Ea, Su0, Su1, Eu, NLb, NLo} = Rn[1] ? 13'h17c3 : 13'bz;  // Driver driver_2
  assign {Cp, Ep, NLm, NCE, NLi, NEi, NLa, Ea, Su0, Su1, Eu, NLb, NLo} = Rn[2] ? 13'h4c3 : 13'bz;  // Driver driver_3
  assign {Cp, Ep, NLm, NCE, NLi, NEi, NLa, Ea, Su0, Su1, Eu, NLb, NLo} = Rn[0] ? 13'hbc3 : 13'bz;  // Driver driver_4
endmodule
