// Digital circuit CustomRingCounter.dig as structural Verilog
module CustomRingCounter (
  input  D,
  input  Clk,
  output [3:0] Out
);

  D_FF d_ff_1 (.D(D), .C(Clk), .Q(Out[0]));  // open: nQ
  D_FF d_ff_2 (.D(Out[0]), .C(Clk), .Q(Out[1]));  // open: nQ
  D_FF d_ff_3 (.D(Out[1]), .C(Clk), .Q(Out[2]));  // open: nQ
  D_FF d_ff_4 (.D(Out[2]), .C(Clk), .Q(Out[3]));  // open: nQ

  // Other names for the same wires on the sheet: Q0 = Out[0]; Q1 = Out[1]; Q2 = Out[2]; Q3 = Out[3]
endmodule
