// Digital circuit Full_adder.dig as structural Verilog
module Full_adder (
  input  I1,
  input  I2,
  input  C0,
  output O,
  output C1
);

  wire and_1_out, and_2_out, and_3_out;

  xor xor_1 (O, I1, C0, I2);
  and and_1 (and_1_out, I1, I2);
  and and_2 (and_2_out, I2, C0);
  and and_3 (and_3_out, I1, C0);
  or or_1 (C1, and_1_out, and_2_out, and_3_out);
endmodule
